// Digital circuit 4_bit_counter.dig as structural Verilog
module _4_bit_counter (
  input  clk
);

  wire jk_ff_1_nq, jk_ff_1_q, jk_ff_2_nq, jk_ff_2_q, jk_ff_3_nq, jk_ff_3_q, jk_ff_4_q;

  LED q3 (.in(jk_ff_4_q));
  JK_FF jk_ff_1 (.J(1'b1), .C(clk), .K(1'b1), .Q(jk_ff_1_q), .nQ(jk_ff_1_nq));
  LED q2 (.in(jk_ff_3_q));
  JK_FF jk_ff_2 (.J(1'b1), .C(jk_ff_1_nq), .K(1'b1), .Q(jk_ff_2_q), .nQ(jk_ff_2_nq));
  JK_FF jk_ff_3 (.J(1'b1), .C(jk_ff_2_nq), .K(1'b1), .Q(jk_ff_3_q), .nQ(jk_ff_3_nq));
  LED q1 (.in(jk_ff_2_q));
  JK_FF jk_ff_4 (.J(1'b1), .C(jk_ff_3_nq), .K(1'b1), .Q(jk_ff_4_q));  // open: nQ
  LED q0 (.in(jk_ff_1_q));
endmodule
