// Digital circuit simple_circuit_instructor.dig as structural Verilog
module simple_circuit_instructor (
  input  A,
  input  B,
  input  C,
  input  D,
  output V
);

  wire and_1_out, and_2_out, not_1_out, or_1_out;

  and and_1 (and_1_out, A, B);
  not not_1 (not_1_out, C);
  or or_1 (or_1_out, and_1_out, not_1_out);
  and and_2 (and_2_out, or_1_out, D);
  not not_2 (V, and_2_out);
endmodule
